// Logisim project main.circ as structural Verilog: 4 circuits, main circuit main
module main (
  output [39:0] out_1,
  output [7:0] out_2,
  output [3:0] out_3,
  output [3:0] out_4,
  output [15:0] out_5,
  output [15:0] out_6,
  output [8:0] out_7
);

  wire ALLOW_WRITE, and_1_out, and_2_out, and_3_out, and_5_out, and_6_out, and_7_out, ARG1_POINTER,
       ARG1_TYPE, ARG2_POINTER, ARG2_TYPE, BEQ, BGT, BLT, BNE, CLK, comparator_1_eq, comparator_2_eq,
       comparator_2_gt, comparator_2_lt, comparator_3_eq, comparator_4_eq, demultiplexer_1_out0,
       demultiplexer_1_out1, demultiplexer_1_out2, demultiplexer_1_out3, demultiplexer_1_out4,
       demultiplexer_2_out1, demultiplexer_3_out0, demultiplexer_3_out1, demultiplexer_3_out2,
       demultiplexer_3_out3, demultiplexer_3_out4, demultiplexer_3_out5, demultiplexer_3_out6,
       demultiplexer_3_out7, demultiplexer_4_out1, demultiplexer_5_out2, demultiplexer_6_out1, FLAG_VALUE,
       MEM_WE, not_1_out, or_2_out, or_3_out, or_4_out, RESET;
  wire [2:0] bit_extender_1_out, bit_extender_2_out, multiplexer_3_out;
  wire [8:0] counter_1_q;
  wire [15:0] adder_1_out, ADDR_MEM, ARG1_REG_VALUE, ARG2_REG_VALUE, CST_R0, CST_R1, divider_1_out,
       get_addr_target_1_out_4, get_addr_target_2_out_4, multiplexer_1_out, multiplexer_6_out,
       multiplexer_8_out, multiplier_1_out, R2_q, R2_RES, R3_q, R4_q, R5_q, R6_q, R7_q, SAVE_VALUE,
       subtractor_1_out, VALUE_MEM_Q;

  Button button_1 (.out(RESET));
  Clock clock_1 (.out(CLK));
  Adder #(.width(16)) adder_1 (.a(CST_R0), .b(CST_R1), .out(adder_1_out));  // open: cin, cout
  Subtractor #(.width(16)) subtractor_1 (.a(CST_R0), .b(CST_R1), .out(subtractor_1_out));  // open: bin, bout
  Multiplier #(.width(16)) multiplier_1 (.a(CST_R0), .b(CST_R1), .out(multiplier_1_out));  // open: cin, cout
  Divider #(.width(16)) divider_1 (.a(CST_R0), .b(CST_R1), .out(divider_1_out));  // open: upper, rem
  Multiplexer #(.width(16)) multiplexer_1 (
    .in0(ARG2_REG_VALUE), .in1({16{1'b0}}), .out(multiplexer_1_out), .sel(out_1[32]));
  is_memaddr is_memaddr_1 (.INT_ARG(out_1[31:16]), .out_2(ARG1_TYPE));
  is_memaddr is_memaddr_2 (.INT_ARG(out_1[15:0]), .out_2(ARG2_TYPE));
  Comparator #(.width(2)) comparator_1 (.a(out_1[37:36]), .b(2'b10), .eq(comparator_1_eq));  // open: gt, lt
  Comparator #(.mode("unsigned"), .width(16)) comparator_2 (
    .a(ARG1_REG_VALUE), .b(multiplexer_1_out), .gt(comparator_2_gt), .eq(comparator_2_eq),
    .lt(comparator_2_lt));
  not not_1 (not_1_out, CLK);
  or or_1 (MEM_WE, ARG2_TYPE, ARG2_POINTER);
  Multiplexer #(.select(2), .width(16)) multiplexer_2 (
    .in0(adder_1_out), .in1(subtractor_1_out), .in2(multiplier_1_out), .in3(divider_1_out), .out(R2_RES),
    .sel(out_1[33:32]));
  Counter #(.max('h1ff), .width(9)) counter_1 (
    .clr(RESET), .load(FLAG_VALUE), .clk(not_1_out), .D(out_1[24:16]), .Q(counter_1_q));  // open: up, count, carry
  is_pointer is_pointer_1 (.REG_ARG(out_1[31:16]), .IS_MEMADDR(ARG1_TYPE), .out_3(ARG1_POINTER));
  is_pointer is_pointer_2 (.REG_ARG(out_1[15:0]), .IS_MEMADDR(ARG2_TYPE), .out_3(ARG2_POINTER));
  and and_1 (and_1_out, comparator_1_eq, CLK);
  D_Flip_Flop u_BGT (.D(comparator_2_gt), .clk(and_1_out), .Q(BGT), .reset(RESET));  // open: Qn, preset
  D_Flip_Flop u_BEQ (.D(comparator_2_eq), .clk(and_1_out), .Q(BEQ), .Qn(BNE), .reset(RESET));  // open: preset
  D_Flip_Flop u_BLT (.D(comparator_2_lt), .clk(and_1_out), .Q(BLT), .reset(RESET));  // open: Qn, preset
  Demultiplexer #(.select(4)) demultiplexer_1 (
    .out0(demultiplexer_1_out0), .out1(demultiplexer_1_out1), .out2(demultiplexer_1_out2),
    .out3(demultiplexer_1_out3), .out4(demultiplexer_1_out4), .in(1'b1), .sel(out_1[35:32]));  // open: out5, out6, out7, out8, out9, out10, out11, out12, out13, out14, out15
  and and_2 (and_2_out, demultiplexer_1_out3, BGT);
  or or_2 (or_2_out, demultiplexer_1_out4, and_2_out, and_3_out, and_5_out, and_6_out);
  Comparator #(.width(2)) comparator_3 (.a(out_1[37:36]), .b(2'b11), .eq(comparator_3_eq));  // open: gt, lt
  ROM #(.addrWidth(9), .dataWidth(40)) PROG (.addr(counter_1_q), .data(out_1));
  Demultiplexer #(.select(2)) demultiplexer_2 (
    .out1(demultiplexer_2_out1), .in(1'b1), .sel(out_1[37:36]));  // open: out0, out2, out3
  and and_3 (and_3_out, demultiplexer_1_out2, BLT);
  and and_4 (FLAG_VALUE, or_2_out, comparator_3_eq);
  Multiplexer #(.width(3)) multiplexer_3 (
    .in0(out_1[2:0]), .in1(3'b010), .out(multiplexer_3_out), .sel(demultiplexer_2_out1));
  and and_5 (and_5_out, demultiplexer_1_out1, BNE);
  and and_6 (and_6_out, demultiplexer_1_out0, BEQ);
  Demultiplexer #(.select(3)) demultiplexer_3 (
    .out0(demultiplexer_3_out0), .out1(demultiplexer_3_out1), .out2(demultiplexer_3_out2),
    .out3(demultiplexer_3_out3), .out4(demultiplexer_3_out4), .out5(demultiplexer_3_out5),
    .out6(demultiplexer_3_out6), .out7(demultiplexer_3_out7), .in(1'b1), .sel(multiplexer_3_out));
  Demultiplexer #(.select(2)) demultiplexer_4 (
    .out1(demultiplexer_4_out1), .in(1'b1), .sel(out_1[37:36]));  // open: out0, out2, out3
  and and_7 (and_7_out, ~ARG2_TYPE, ~ARG2_POINTER, ALLOW_WRITE);  // AND_Gate
  Register #(.trigger("high"), .width(16)) R0 (
    .D(SAVE_VALUE), .en(demultiplexer_3_out0), .clk(and_7_out), .Q(CST_R0), .clr(RESET));
  Register #(.trigger("high"), .width(16)) R1 (
    .D(SAVE_VALUE), .en(demultiplexer_3_out1), .clk(and_7_out), .Q(CST_R1), .clr(RESET));
  Register #(.trigger("high"), .width(16)) R2 (
    .D(SAVE_VALUE), .en(demultiplexer_3_out2), .clk(and_7_out), .Q(R2_q), .clr(RESET));
  Register #(.trigger("high"), .width(16)) R3 (
    .D(SAVE_VALUE), .en(demultiplexer_3_out3), .clk(and_7_out), .Q(R3_q), .clr(RESET));
  Register #(.trigger("high"), .width(16)) R4 (
    .D(SAVE_VALUE), .en(demultiplexer_3_out4), .clk(and_7_out), .Q(R4_q), .clr(RESET));
  Register #(.trigger("high"), .width(16)) R5 (
    .D(SAVE_VALUE), .en(demultiplexer_3_out5), .clk(and_7_out), .Q(R5_q), .clr(RESET));
  Register #(.trigger("high"), .width(16)) R6 (
    .D(SAVE_VALUE), .en(demultiplexer_3_out6), .clk(and_7_out), .Q(R6_q), .clr(RESET));
  Register #(.trigger("high"), .width(16)) R7 (
    .D(SAVE_VALUE), .en(demultiplexer_3_out7), .clk(and_7_out), .Q(R7_q), .clr(RESET));
  Comparator #(.width(4)) comparator_4 (.a(out_1[39:36]), .b(4'b0000), .eq(comparator_4_eq));  // open: gt, lt
  or or_3 (or_3_out, comparator_4_eq, demultiplexer_4_out1);
  Multiplexer #(.select(3), .width(16)) multiplexer_4 (
    .in0(CST_R0), .in1(CST_R1), .in2(R2_q), .in3(R3_q), .in4(R4_q), .in5(R5_q), .in6(R6_q), .in7(R7_q),
    .out(ARG1_REG_VALUE), .sel(bit_extender_1_out));
  Multiplexer #(.select(3), .width(16)) multiplexer_5 (
    .in0(CST_R0), .in1(CST_R1), .in2(R2_q), .in3(R3_q), .in4(R4_q), .in5(R5_q), .in6(R6_q), .in7(R7_q),
    .out(ARG2_REG_VALUE), .sel(bit_extender_2_out));
  and and_8 (ALLOW_WRITE, or_3_out, CLK);
  Bit_Extender #(.in_width(16), .out_width(3)) bit_extender_1 (.in(out_1[31:16]), .out(bit_extender_1_out));
  or or_4 (or_4_out, ARG1_TYPE, ARG1_POINTER);
  Bit_Extender #(.in_width(16), .out_width(3)) bit_extender_2 (.in(out_1[15:0]), .out(bit_extender_2_out));
  RAM #(.addrWidth(16), .dataWidth(16)) MEMORY (
    .addr(ADDR_MEM), .we(MEM_WE), .oe(1'b1), .clk(ALLOW_WRITE), .din(SAVE_VALUE), .dout(VALUE_MEM_Q));
  get_addr_target get_addr_target_1 (
    .INT_ARG(out_1[31:16]), .REG_VALUE(ARG1_REG_VALUE), .IS_POINTER(ARG1_POINTER),
    .out_4(get_addr_target_1_out_4));
  get_addr_target get_addr_target_2 (
    .INT_ARG(out_1[15:0]), .REG_VALUE(ARG2_REG_VALUE), .IS_POINTER(ARG2_POINTER),
    .out_4(get_addr_target_2_out_4));
  Multiplexer #(.width(16)) multiplexer_6 (
    .in0(ARG1_REG_VALUE), .in1(VALUE_MEM_Q), .out(multiplexer_6_out), .sel(or_4_out));
  Demultiplexer #(.select(2)) demultiplexer_5 (
    .out2(demultiplexer_5_out2), .in(1'b1), .sel(out_1[33:32]));  // open: out0, out1, out3
  Demultiplexer #(.select(2)) demultiplexer_6 (
    .out1(demultiplexer_6_out1), .in(1'b1), .sel(out_1[37:36]));  // open: out0, out2, out3
  Multiplexer #(.width(16)) multiplexer_7 (
    .in0(get_addr_target_1_out_4), .in1(get_addr_target_2_out_4), .out(ADDR_MEM), .sel(MEM_WE));
  Multiplexer #(.width(16)) multiplexer_8 (
    .in0(multiplexer_6_out), .in1(out_1[31:16]), .out(multiplexer_8_out), .sel(demultiplexer_5_out2));
  // Probe on VALUE_MEM_Q
  Multiplexer #(.width(16)) multiplexer_9 (
    .in0(multiplexer_8_out), .in1(R2_RES), .out(SAVE_VALUE), .sel(demultiplexer_6_out1));

  assign out_2 = out_1[39:32];
  assign out_3 = out_1[39:36];
  assign out_4 = out_1[35:32];
  assign out_5 = out_1[31:16];
  assign out_6 = out_1[15:0];

  // Other names for the same wires on the sheet: INT_ARG2[15:0] = out_1[15:0]; INT_BITFIELD[39:0] = out_1;
  //   INT_ARG1[15:0] = out_1[31:16]; INT_OP_TYPE2[3:0] = out_1[35:32]; INT_OPCODE[7:0] = out_1[39:32];
  //   INT_OP_TYPE1[3:0] = out_1[39:36]; INT_COUNTER[8:0] = out_7

  // Notes on the sheet:
  //   contents of PROG (hex, n*v repeats v):
  //   200050000 200010001 2001f0006 200200003 1100000000 100020013 100130007 100130016 100020004 100030000
  //   1000000000 100020003 100040000 2100000000 3100040000 100030000 1000000000 2abcd0012
endmodule

module is_memaddr (
  input  [15:0] INT_ARG,
  output out_2
);

  wire comparator_1_eq, comparator_1_gt;

  Comparator #(.width(16)) comparator_1 (
    .a(INT_ARG), .b(16'h20), .gt(comparator_1_gt), .eq(comparator_1_eq));  // open: lt
  or or_1 (out_2, comparator_1_gt, comparator_1_eq);
endmodule

module is_pointer (
  input  [15:0] REG_ARG,
  input  IS_MEMADDR,
  output out_3
);

  and and_1 (out_3, REG_ARG[4], ~IS_MEMADDR);  // AND_Gate
endmodule

module get_addr_target (
  input  [15:0] INT_ARG,
  input  [15:0] REG_VALUE,
  input  IS_POINTER,
  output [15:0] out_4
);

  Multiplexer #(.width(16)) multiplexer_1 (.in0(INT_ARG), .in1(REG_VALUE), .out(out_4), .sel(IS_POINTER));
endmodule
